// Logisim project TP.circ as structural Verilog: 27 circuits, main circuit main
module main (
  input  in_1
);

  wire alu_4_1_cout, alu_4_1_null, CLK, FETCH, not_1_out, unitee_controle_1_ad_write,
       unitee_controle_1_alu_to_reg, unitee_controle_1_f0, unitee_controle_1_f1, unitee_controle_1_f2,
       unitee_controle_1_pc_write, unitee_controle_1_r0a, unitee_controle_1_r0b, unitee_controle_1_r1a,
       unitee_controle_1_r1b, unitee_controle_1_r2a, unitee_controle_1_r2b, unitee_controle_1_r3a,
       unitee_controle_1_r3b, unitee_controle_1_ram_to_reg, unitee_controle_1_reg_to_ram,
       unitee_controle_1_w0, unitee_controle_1_w1, unitee_controle_1_w2, unitee_controle_1_w3;
  wire [3:0] alu_4_1_s, banc_registre_4_4_1_a, banc_registre_4_4_1_b, controlled_buffer_1_out,
       controlled_buffer_2_out, ram_4b_16l_1_data_out, unite_adressage_1_ad_out, unite_adressage_1_pc_out,
       unitee_controle_1_ad_out, unitee_controle_1_pc_out;
  wire [11:0] ram_12b_16l_1_data_out;

  RAM_4b_16l ram_4b_16l_1 (
    .addr(unite_adressage_1_ad_out), .CLK(CLK), .ld___nread(not_1_out), .data_in(controlled_buffer_1_out),
    .data_out(ram_4b_16l_1_data_out));
  not not_1 (not_1_out, unitee_controle_1_reg_to_ram);
  RAM_12b_16l ram_12b_16l_1 (
    .addr(unite_adressage_1_pc_out), .CLK(CLK), .ld___nread(FETCH), .data_out(ram_12b_16l_1_data_out));  // open: data_in
  // Probe on banc_registre_4_4_1_a
  assign controlled_buffer_1_out = unitee_controle_1_reg_to_ram ? banc_registre_4_4_1_a : 4'bz;  // Controlled_Buffer controlled_buffer_1
  // Probe on ram_4b_16l_1_data_out
  // Probe on unite_adressage_1_ad_out
  // Probe on unite_adressage_1_pc_out
  // Probe on ram_12b_16l_1_data_out
  Clock clock_1 (.out(CLK));
  assign controlled_buffer_2_out = unitee_controle_1_ram_to_reg ? ram_4b_16l_1_data_out : 4'bz;  // Controlled_Buffer controlled_buffer_2
  assign controlled_buffer_2_out = unitee_controle_1_alu_to_reg ? alu_4_1_s : 4'bz;  // Controlled_Buffer controlled_buffer_3
  UNITE_ADRESSAGE unite_adressage_1 (
    .AD_in(unitee_controle_1_ad_out), .AD_w(unitee_controle_1_ad_write), .PC_in(unitee_controle_1_pc_out),
    .PC_w(unitee_controle_1_pc_write), .CLK(CLK), .AD_OUT(unite_adressage_1_ad_out),
    .PC_OUT(unite_adressage_1_pc_out));  // open: ext0, ext1
  BANC_REGISTRE_4_4 banc_registre_4_4_1 (
    .DATA_IN(controlled_buffer_2_out), .w0(unitee_controle_1_w0), .w1(unitee_controle_1_w1),
    .w2(unitee_controle_1_w2), .w3(unitee_controle_1_w3), .A(banc_registre_4_4_1_a),
    .B(banc_registre_4_4_1_b), .CLK(CLK), .a0(unitee_controle_1_r0a), .a1(unitee_controle_1_r1a),
    .a2(unitee_controle_1_r2a), .a3(unitee_controle_1_r3a), .b0(unitee_controle_1_r0b),
    .b1(unitee_controle_1_r1b), .b3(unitee_controle_1_r2b), .b4(unitee_controle_1_r3b));  // open: ext1, ext2
  UNITEE_CONTROLE unitee_controle_1 (
    .data_in(ram_12b_16l_1_data_out), .RESET(in_1), .w0(unitee_controle_1_w0), .w1(unitee_controle_1_w1),
    .w2(unitee_controle_1_w2), .w3(unitee_controle_1_w3), .r0a(unitee_controle_1_r0a),
    .r1a(unitee_controle_1_r1a), .r2a(unitee_controle_1_r2a), .r3a(unitee_controle_1_r3a),
    .r0b(unitee_controle_1_r0b), .r1b(unitee_controle_1_r1b), .r2b(unitee_controle_1_r2b),
    .r3b(unitee_controle_1_r3b), .fetch(FETCH), .CLK(CLK), .PC_in(unite_adressage_1_pc_out),
    .PC_out(unitee_controle_1_pc_out), .PC_write(unitee_controle_1_pc_write),
    .AD_out(unitee_controle_1_ad_out), .AD_write(unitee_controle_1_ad_write), .f0(unitee_controle_1_f0),
    .f1(unitee_controle_1_f1), .ram_to_reg(unitee_controle_1_ram_to_reg),
    .reg_to_ram(unitee_controle_1_reg_to_ram), .alu_to_reg(unitee_controle_1_alu_to_reg),
    .f2(unitee_controle_1_f2));  // open: N_C, N_C_2
  // Probe on unitee_controle_1_ad_out
  // Probe on banc_registre_4_4_1_a
  // Probe on banc_registre_4_4_1_b
  ALU_4 alu_4_1 (
    .B(banc_registre_4_4_1_b), .Cin(1'b0), .A(banc_registre_4_4_1_a), .sel0(unitee_controle_1_f0),
    .sel1(unitee_controle_1_f1), .sel2(unitee_controle_1_f2), .S(alu_4_1_s), .Cout(alu_4_1_cout),
    .NULL(alu_4_1_null));  // open: ext1, ext2, ext3
  // Probe on alu_4_1_s
  LED led_1 (.in(alu_4_1_null));
  LED led_2 (.in(alu_4_1_cout));
endmodule

module MUX_2_1 (
  input  e1,
  input  e0,
  input  Sel0,
  output S
);

  wire and_1_out, and_2_out, not_1_out;

  not not_1 (not_1_out, Sel0);
  and and_1 (and_1_out, e1, Sel0);
  and and_2 (and_2_out, not_1_out, e0);
  or or_1 (S, and_1_out, and_2_out);
endmodule

module HALF_ADDER (
  input  e0,
  input  e1,
  output S,
  output R
);

  XOR xor_1 (.e0(e0), .e1(e1), .S(S));
  and and_1 (R, e0, e1);
endmodule

module FULL_ADDER (
  input  Ri,
  input  e0,
  input  e1,
  output S,
  output Re
);

  wire and_1_out, half_adder_1_r, half_adder_1_s;

  HALF_ADDER half_adder_1 (.e0(e0), .e1(e1), .S(half_adder_1_s), .R(half_adder_1_r));
  or or_1 (Re, half_adder_1_r, and_1_out);
  and and_1 (and_1_out, half_adder_1_s, Ri);
  XOR xor_1 (.e0(half_adder_1_s), .e1(Ri), .S(S));
endmodule

module XOR (
  input  e0,
  input  e1,
  output S
);

  wire and_1_out, not_1_out, or_1_out;

  or or_1 (or_1_out, e0, e1);
  not not_1 (not_1_out, and_1_out);
  and and_1 (and_1_out, e1, e0);
  and and_2 (S, or_1_out, not_1_out);
endmodule

module MUX_8_1 (
  input  in_1,
  input  in_2,
  input  in_3,
  input  in_4,
  input  in_5,
  input  in_6,
  input  in_7,
  input  in_8,
  input  in_9,
  input  in_10,
  input  in_11,
  output out_12
);

  wire and_1_out, and_2_out, and_3_out, and_4_out, and_5_out, and_6_out, and_7_out, and_8_out, not_1_out,
       not_2_out, not_3_out;

  not not_1 (not_1_out, in_1);
  not not_2 (not_2_out, in_2);
  not not_3 (not_3_out, in_3);
  and and_1 (and_1_out, in_4, not_3_out, not_2_out, not_1_out);
  and and_2 (and_2_out, in_5, in_3, not_2_out, not_1_out);
  and and_3 (and_3_out, in_6, not_3_out, in_2, not_1_out);
  and and_4 (and_4_out, in_7, in_3, in_2, not_1_out);
  and and_5 (and_5_out, in_8, not_3_out, not_2_out, in_1);
  and and_6 (and_6_out, in_9, in_3, not_2_out, in_1);
  and and_7 (and_7_out, in_10, not_3_out, in_2, in_1);
  and and_8 (and_8_out, in_11, in_3, in_2, in_1);
  or or_1 (out_12, and_1_out, and_2_out, and_3_out, and_4_out, and_5_out, and_6_out, and_7_out, and_8_out);
endmodule

module MUX_8_1_B (
  input  [7:0] data,
  input  [2:0] Sel,
  output S
);

  MUX_8_1 mux_8_1_1 (
    .in_4(data[0]), .in_5(data[1]), .in_6(data[2]), .in_7(data[3]), .in_8(data[4]), .in_9(data[5]),
    .in_10(data[6]), .in_11(data[7]), .out_12(S), .in_1(Sel[0]), .in_2(Sel[1]), .in_3(Sel[2]));
endmodule

module DEC_3_8 (
  input  e2,
  input  e1,
  input  e0,
  output s0,
  output s1,
  output s2,
  output s3,
  output s4,
  output s5,
  output s6,
  output s7
);

  wire not_1_out, not_2_out, not_3_out;

  not not_1 (not_1_out, e2);
  not not_2 (not_2_out, e1);
  not not_3 (not_3_out, e0);
  and and_1 (s0, not_1_out, not_2_out, not_3_out);
  and and_2 (s1, not_1_out, not_2_out, e0);
  and and_3 (s2, not_1_out, e1, not_3_out);
  and and_4 (s3, not_1_out, e1, e0);
  and and_5 (s4, e2, not_2_out, not_3_out);
  and and_6 (s5, e2, not_2_out, e0);
  and and_7 (s6, e2, e1, not_3_out);
  and and_8 (s7, e2, e1, e0);
endmodule

module DEC_4_16 (
  input  e3,
  input  e2,
  input  e1,
  input  e0,
  input  En,
  output s0,
  output s1,
  output s2,
  output s3,
  output s4,
  output s5,
  output s6,
  output s7,
  output s8,
  output s9,
  output s10,
  output s11,
  output s12,
  output s13,
  output s14,
  output s15
);

  wire and_1_out, and_2_out, and_3_out, and_4_out, and_5_out, and_6_out, and_7_out, and_8_out, and_9_out,
       and_10_out, and_11_out, and_12_out, and_13_out, and_14_out, and_15_out, and_16_out, not_1_out,
       not_2_out, not_3_out, not_4_out;

  not not_1 (not_1_out, e3);
  not not_2 (not_2_out, e2);
  not not_3 (not_3_out, e1);
  not not_4 (not_4_out, e0);
  and and_1 (and_1_out, not_4_out, not_3_out, not_2_out, not_1_out);
  and and_2 (and_2_out, e0, not_3_out, not_2_out, not_1_out);
  and and_3 (and_3_out, not_4_out, e1, not_2_out, not_1_out);
  and and_4 (and_4_out, e0, e1, not_2_out, not_1_out);
  and and_5 (and_5_out, not_4_out, not_3_out, e2, not_1_out);
  and and_6 (and_6_out, e0, not_3_out, e2, not_1_out);
  and and_7 (and_7_out, not_4_out, e1, e2, not_1_out);
  and and_8 (and_8_out, e0, e1, e2, not_1_out);
  and and_9 (and_9_out, not_4_out, not_3_out, not_2_out, e3);
  and and_10 (and_10_out, e0, not_3_out, not_2_out, e3);
  and and_11 (and_11_out, not_4_out, e1, not_2_out, e3);
  and and_12 (and_12_out, e0, e1, not_2_out, e3);
  and and_13 (and_13_out, not_4_out, not_3_out, e2, e3);
  and and_14 (and_14_out, e0, not_3_out, e2, e3);
  and and_15 (and_15_out, not_4_out, e1, e2, e3);
  and and_16 (and_16_out, e0, e1, e2, e3);
  and and_17 (s0, En, and_1_out);
  and and_18 (s1, En, and_2_out);
  and and_19 (s2, En, and_3_out);
  and and_20 (s3, En, and_4_out);
  and and_21 (s4, En, and_5_out);
  and and_22 (s5, En, and_6_out);
  and and_23 (s6, En, and_7_out);
  and and_24 (s7, En, and_8_out);
  and and_25 (s8, En, and_9_out);
  and and_26 (s9, En, and_10_out);
  and and_27 (s10, En, and_11_out);
  and and_28 (s11, En, and_12_out);
  and and_29 (s12, En, and_13_out);
  and and_30 (s13, En, and_14_out);
  and and_31 (s14, En, and_15_out);
  and and_32 (s15, En, and_16_out);
endmodule

module DEC_5_32 (
  input  e0,
  input  e1,
  input  e2,
  input  e3,
  input  e4,
  input  enable,
  output s0,
  output s1,
  output s2,
  output s3,
  output s4,
  output s5,
  output s6,
  output s7,
  output s8,
  output s9,
  output s10,
  output s11,
  output s12,
  output s13,
  output s14,
  output s15,
  output s16,
  output s17,
  output s18,
  output s19,
  output s20,
  output s21,
  output s22,
  output s23,
  output s24,
  output s25,
  output s26,
  output s27,
  output s28,
  output s29,
  output s30,
  output s31
);

  wire and_1_out, and_2_out, not_1_out;

  not not_1 (not_1_out, e4);
  and and_1 (and_1_out, not_1_out, enable);
  and and_2 (and_2_out, enable, e4);
  DEC_4_16 dec_4_16_1 (
    .s0(s0), .s1(s1), .s2(s2), .s3(s3), .s4(s4), .s5(s5), .s6(s6), .s7(s7), .s8(s8), .s9(s9), .s10(s10),
    .s11(s11), .s12(s12), .s13(s13), .s14(s14), .s15(s15), .e3(e3), .e2(e2), .e1(e1), .e0(e0), .En(and_1_out));
  DEC_4_16 dec_4_16_2 (
    .s0(s16), .s1(s17), .s2(s18), .s3(s19), .s4(s20), .s5(s21), .s6(s22), .s7(s23), .s8(s24), .s9(s25),
    .s10(s26), .s11(s27), .s12(s28), .s13(s29), .s14(s30), .s15(s31), .e3(e3), .e2(e2), .e1(e1), .e0(e0),
    .En(and_2_out));
endmodule

module COMP_4 (
  input  [3:0] A,
  input  [3:0] B,
  output S
);

  wire or_1_out, xor_1_s, xor_2_s, xor_3_s, xor_4_s;

  XOR xor_1 (.e0(B[0]), .e1(A[0]), .S(xor_1_s));
  XOR xor_2 (.e0(B[1]), .e1(A[1]), .S(xor_2_s));
  XOR xor_3 (.e0(B[2]), .e1(A[2]), .S(xor_3_s));
  XOR xor_4 (.e0(B[3]), .e1(A[3]), .S(xor_4_s));
  or or_1 (or_1_out, xor_1_s, xor_2_s, xor_3_s, xor_4_s);
  not not_1 (S, or_1_out);
endmodule

module ALU_1 (
  input  Cin,
  input  A,
  input  B,
  input  sel0,
  input  sel1,
  input  sel2,
  output Cout,
  output S
);

  wire and_1_out, and_2_out, and_4_out, and_5_out, and_6_out, dec_3_8_1_s0, dec_3_8_1_s1, dec_3_8_1_s2,
       dec_3_8_1_s3, full_adder_1_re, full_adder_1_s, not_1_out, or_1_out;

  DEC_3_8 dec_3_8_1 (
    .s0(dec_3_8_1_s0), .s1(dec_3_8_1_s1), .s2(dec_3_8_1_s2), .s3(dec_3_8_1_s3), .e2(sel2), .e1(sel1),
    .e0(sel0));  // open: s4, s5, s6, s7
  or or_1 (or_1_out, A, B);
  and and_1 (and_1_out, A, B);
  not not_1 (not_1_out, B);
  FULL_ADDER full_adder_1 (.e0(A), .e1(B), .S(full_adder_1_s), .Ri(Cin), .Re(full_adder_1_re));
  and and_2 (and_2_out, full_adder_1_s, dec_3_8_1_s0);
  and and_3 (Cout, dec_3_8_1_s0, full_adder_1_re);
  and and_4 (and_4_out, or_1_out, dec_3_8_1_s1);
  and and_5 (and_5_out, and_1_out, dec_3_8_1_s2);
  and and_6 (and_6_out, not_1_out, dec_3_8_1_s3);
  or or_2 (S, and_2_out, and_4_out, and_5_out, and_6_out);
endmodule

module ALU_4 (
  input  [3:0] B,
  input  Cin,
  input  [3:0] A,
  input  sel0,
  input  sel1,
  input  sel2,
  output [3:0] S,
  output Cout,
  output NULL,
  output ext1,
  output ext2,
  output ext3
);

  wire alu_1_2_cout, alu_1_3_cout, alu_1_4_cout, and_1_out, comp_4_1_s, controlled_buffer_3_out, not_2_out,
       not_3_out;
  wire [3:0] controlled_buffer_1_out, not_1_out;

  assign not_1_out = ~B;  // NOT_Gate not_1, 4 bits wide
  assign controlled_buffer_1_out = not_2_out ? B : 4'bz;  // Controlled_Buffer controlled_buffer_1
  not not_2 (not_2_out, and_1_out);
  assign controlled_buffer_1_out = and_1_out ? not_1_out : 4'bz;  // Controlled_Buffer controlled_buffer_2
  not not_3 (not_3_out, and_1_out);
  and and_1 (and_1_out, sel2, ~sel1, ~sel0);  // AND_Gate
  assign controlled_buffer_3_out = and_1_out ? and_1_out : 1'bz;  // Controlled_Buffer controlled_buffer_3
  assign controlled_buffer_3_out = not_3_out ? Cin : 1'bz;  // Controlled_Buffer controlled_buffer_4
  ALU_1 alu_1_1 (
    .A(A[3]), .B(controlled_buffer_1_out[3]), .sel0(sel0), .sel1(sel1), .sel2(1'b0), .Cout(Cout), .S(S[3]),
    .Cin(alu_1_2_cout));
  COMP_4 comp_4_1 (.S(comp_4_1_s), .A(B), .B(A));
  and and_2 (NULL, and_1_out, comp_4_1_s);
  ALU_1 alu_1_2 (
    .A(A[2]), .B(controlled_buffer_1_out[2]), .sel0(sel0), .sel1(sel1), .sel2(1'b0), .Cout(alu_1_2_cout),
    .S(S[2]), .Cin(alu_1_3_cout));
  ALU_1 alu_1_3 (
    .A(A[1]), .B(controlled_buffer_1_out[1]), .sel0(sel0), .sel1(sel1), .sel2(1'b0), .Cout(alu_1_3_cout),
    .S(S[1]), .Cin(alu_1_4_cout));
  ALU_1 alu_1_4 (
    .A(A[0]), .B(controlled_buffer_1_out[0]), .sel0(sel0), .sel1(sel1), .sel2(1'b0), .Cout(alu_1_4_cout),
    .S(S[0]), .Cin(controlled_buffer_3_out));

  // Notes on the sheet:
  //   Soustraction
endmodule

module bascule_D_1 (
  input  CLK,
  input  D,
  output Q,
  output nQ
);

  D_Flip_Flop d_ff_1 (.clk(CLK), .D(D), .Q(Q), .Qn(nQ));  // open: preset, en, reset
endmodule

module REGISTRE_4 (
  input  [3:0] data_in,
  input  write,
  input  CLK,
  input  read,
  output [3:0] data_out
);

  wire bascule_d_1_1_q, bascule_d_1_2_q, bascule_d_1_3_q, bascule_d_1_4_q, controlled_buffer_1_out,
       controlled_buffer_2_out, controlled_buffer_3_out, controlled_buffer_4_out;

  assign controlled_buffer_1_out = write ? data_in[0] : 1'bz;  // Controlled_Buffer controlled_buffer_1
  assign controlled_buffer_2_out = write ? data_in[1] : 1'bz;  // Controlled_Buffer controlled_buffer_2
  assign controlled_buffer_3_out = write ? data_in[2] : 1'bz;  // Controlled_Buffer controlled_buffer_3
  assign controlled_buffer_4_out = write ? data_in[3] : 1'bz;  // Controlled_Buffer controlled_buffer_4
  bascule_D_1 bascule_d_1_1 (.D(controlled_buffer_1_out), .CLK(CLK), .Q(bascule_d_1_1_q));  // open: nQ
  bascule_D_1 bascule_d_1_2 (.D(controlled_buffer_2_out), .CLK(CLK), .Q(bascule_d_1_2_q));  // open: nQ
  bascule_D_1 bascule_d_1_3 (.D(controlled_buffer_3_out), .CLK(CLK), .Q(bascule_d_1_3_q));  // open: nQ
  bascule_D_1 bascule_d_1_4 (.D(controlled_buffer_4_out), .CLK(CLK), .Q(bascule_d_1_4_q));  // open: nQ
  assign data_out[0] = read ? bascule_d_1_1_q : 1'bz;  // Controlled_Buffer controlled_buffer_5
  assign data_out[1] = read ? bascule_d_1_2_q : 1'bz;  // Controlled_Buffer controlled_buffer_6
  assign data_out[2] = read ? bascule_d_1_3_q : 1'bz;  // Controlled_Buffer controlled_buffer_7
  assign data_out[3] = read ? bascule_d_1_4_q : 1'bz;  // Controlled_Buffer controlled_buffer_8

  // Notes on the sheet:
  //   data_out: pull=up
endmodule

module REGISTRE_12 (
  input  CLK,
  input  [11:0] IN,
  input  Write,
  input  Read,
  output [11:0] OUT
);

  REGISTRE_4 registre_4_1 (.data_in(IN[3:0]), .write(Write), .data_out(OUT[3:0]), .CLK(CLK), .read(Read));
  REGISTRE_4 registre_4_2 (.data_in(IN[7:4]), .write(Write), .data_out(OUT[7:4]), .CLK(CLK), .read(Read));
  REGISTRE_4 registre_4_3 (.data_in(IN[11:8]), .write(Write), .data_out(OUT[11:8]), .CLK(CLK), .read(Read));
endmodule

module BANC_REGISTRE_4_4 (
  input  CLK,
  input  [3:0] DATA_IN,
  input  w0,
  input  w1,
  input  w2,
  input  w3,
  input  a0,
  input  a1,
  input  a2,
  input  a3,
  input  b0,
  input  b1,
  input  b3,
  input  b4,
  output [3:0] A,
  output [3:0] B,
  output ext1,
  output ext2
);

  wire or_1_out, or_2_out, or_3_out, or_4_out;
  wire [3:0] registre_4_1_data_out, registre_4_2_data_out, registre_4_3_data_out, registre_4_4_data_out;

  or or_1 (or_1_out, a2, b3);
  or or_2 (or_2_out, a0, b0);
  or or_3 (or_3_out, a1, b1);
  or or_4 (or_4_out, a3, b4);
  // Probe on registre_4_1_data_out
  REGISTRE_4 registre_4_1 (.data_in(DATA_IN), .write(w0), .data_out(registre_4_1_data_out), .CLK(CLK), .read(or_2_out));
  // Probe on registre_4_2_data_out
  REGISTRE_4 registre_4_2 (.data_in(DATA_IN), .write(w1), .data_out(registre_4_2_data_out), .CLK(CLK), .read(or_3_out));
  // Probe on registre_4_3_data_out
  REGISTRE_4 registre_4_3 (.data_in(DATA_IN), .write(w2), .data_out(registre_4_3_data_out), .CLK(CLK), .read(or_1_out));
  // Probe on registre_4_4_data_out
  REGISTRE_4 registre_4_4 (.data_in(DATA_IN), .write(w3), .data_out(registre_4_4_data_out), .CLK(CLK), .read(or_4_out));
  assign A = a0 ? registre_4_1_data_out : 4'bz;  // Controlled_Buffer controlled_buffer_1
  assign A = a1 ? registre_4_2_data_out : 4'bz;  // Controlled_Buffer controlled_buffer_2
  assign A = a2 ? registre_4_3_data_out : 4'bz;  // Controlled_Buffer controlled_buffer_3
  assign A = a3 ? registre_4_4_data_out : 4'bz;  // Controlled_Buffer controlled_buffer_4
  assign B = b0 ? registre_4_1_data_out : 4'bz;  // Controlled_Buffer controlled_buffer_5
  assign B = b1 ? registre_4_2_data_out : 4'bz;  // Controlled_Buffer controlled_buffer_6
  assign B = b3 ? registre_4_3_data_out : 4'bz;  // Controlled_Buffer controlled_buffer_7
  assign B = b4 ? registre_4_4_data_out : 4'bz;  // Controlled_Buffer controlled_buffer_8

  // Notes on the sheet:
  //   Selection Ecriture
  //   Selection Lecture Bus A
  //   Selection Lecture Bus B
endmodule

module BANC_REGISTRE_12b_4 (
  input  CLK,
  input  [11:0] DATA_IN,
  input  w0,
  input  w1,
  input  w2,
  input  w3,
  input  a0,
  input  a1,
  input  a2,
  input  a3,
  input  b0,
  input  b1,
  input  b3,
  input  b4,
  output [11:0] A,
  output [11:0] B
);

  wire or_1_out, or_2_out, or_3_out, or_4_out;
  wire [11:0] registre_12_1_out, registre_12_2_out, registre_12_3_out, registre_12_4_out;

  or or_1 (or_1_out, a2, b3);
  or or_2 (or_2_out, a1, b1);
  or or_3 (or_3_out, a0, b0);
  or or_4 (or_4_out, a3, b4);
  // Probe on registre_12_1_out
  REGISTRE_12 registre_12_1 (.IN(DATA_IN), .Write(w0), .Read(or_3_out), .OUT(registre_12_1_out), .CLK(CLK));
  // Probe on registre_12_2_out
  REGISTRE_12 registre_12_2 (.IN(DATA_IN), .Write(w1), .Read(or_2_out), .OUT(registre_12_2_out), .CLK(CLK));
  // Probe on registre_12_3_out
  REGISTRE_12 registre_12_3 (.IN(DATA_IN), .Write(w2), .Read(or_1_out), .OUT(registre_12_3_out), .CLK(CLK));
  // Probe on registre_12_4_out
  REGISTRE_12 registre_12_4 (.IN(DATA_IN), .Write(w3), .Read(or_4_out), .OUT(registre_12_4_out), .CLK(CLK));
  assign A = a0 ? registre_12_1_out : 12'bz;  // Controlled_Buffer controlled_buffer_1
  assign A = a1 ? registre_12_2_out : 12'bz;  // Controlled_Buffer controlled_buffer_2
  assign A = a2 ? registre_12_3_out : 12'bz;  // Controlled_Buffer controlled_buffer_3
  assign A = a3 ? registre_12_4_out : 12'bz;  // Controlled_Buffer controlled_buffer_4
  assign B = b0 ? registre_12_1_out : 12'bz;  // Controlled_Buffer controlled_buffer_5
  assign B = b1 ? registre_12_2_out : 12'bz;  // Controlled_Buffer controlled_buffer_6
  assign B = b3 ? registre_12_3_out : 12'bz;  // Controlled_Buffer controlled_buffer_7
  assign B = b4 ? registre_12_4_out : 12'bz;  // Controlled_Buffer controlled_buffer_8

  // Notes on the sheet:
  //   Selection Ecriture
  //   Selection Lecture Bus A
  //   Selection Lecture Bus B
endmodule

module MEMOIRE_4b_16l (
  input  in_1,
  input  in_2,
  input  in_3,
  input  in_4,
  input  in_5,
  input  [3:0] in_6,
  input  CLK,
  input  in_8,
  input  in_9,
  input  in_10,
  input  in_11,
  input  in_12,
  output [3:0] out_13
);

  wire dec_4_16_1_s0, dec_4_16_1_s1, dec_4_16_1_s2, dec_4_16_1_s3, dec_4_16_1_s4, dec_4_16_1_s5,
       dec_4_16_1_s6, dec_4_16_1_s7, dec_4_16_1_s8, dec_4_16_1_s9, dec_4_16_1_s10, dec_4_16_1_s11,
       dec_4_16_1_s12, dec_4_16_1_s13, dec_4_16_1_s14, dec_4_16_1_s15, dec_4_16_2_s0, dec_4_16_2_s1,
       dec_4_16_2_s2, dec_4_16_2_s3, dec_4_16_2_s4, dec_4_16_2_s5, dec_4_16_2_s6, dec_4_16_2_s7,
       dec_4_16_2_s8, dec_4_16_2_s9, dec_4_16_2_s10, dec_4_16_2_s11, dec_4_16_2_s12, dec_4_16_2_s13,
       dec_4_16_2_s14, dec_4_16_2_s15;

  DEC_4_16 dec_4_16_1 (
    .s0(dec_4_16_1_s0), .s1(dec_4_16_1_s1), .s2(dec_4_16_1_s2), .s3(dec_4_16_1_s3), .s4(dec_4_16_1_s4),
    .s5(dec_4_16_1_s5), .s6(dec_4_16_1_s6), .s7(dec_4_16_1_s7), .s8(dec_4_16_1_s8), .s9(dec_4_16_1_s9),
    .s10(dec_4_16_1_s10), .s11(dec_4_16_1_s11), .s12(dec_4_16_1_s12), .s13(dec_4_16_1_s13),
    .s14(dec_4_16_1_s14), .s15(dec_4_16_1_s15), .e3(in_4), .e2(in_3), .e1(in_2), .e0(in_1), .En(in_5));
  DEC_4_16 dec_4_16_2 (
    .s0(dec_4_16_2_s0), .s1(dec_4_16_2_s1), .s2(dec_4_16_2_s2), .s3(dec_4_16_2_s3), .s4(dec_4_16_2_s4),
    .s5(dec_4_16_2_s5), .s6(dec_4_16_2_s6), .s7(dec_4_16_2_s7), .s8(dec_4_16_2_s8), .s9(dec_4_16_2_s9),
    .s10(dec_4_16_2_s10), .s11(dec_4_16_2_s11), .s12(dec_4_16_2_s12), .s13(dec_4_16_2_s13),
    .s14(dec_4_16_2_s14), .s15(dec_4_16_2_s15), .e3(in_11), .e2(in_10), .e1(in_9), .e0(in_8), .En(in_12));
  REGISTRE_4 registre_4_1 (.data_in(in_6), .write(dec_4_16_1_s0), .data_out(out_13), .CLK(CLK), .read(dec_4_16_2_s0));
  REGISTRE_4 registre_4_2 (.data_in(in_6), .write(dec_4_16_1_s8), .data_out(out_13), .CLK(CLK), .read(dec_4_16_2_s8));
  REGISTRE_4 registre_4_3 (.data_in(in_6), .write(dec_4_16_1_s1), .data_out(out_13), .CLK(CLK), .read(dec_4_16_2_s1));
  REGISTRE_4 registre_4_4 (.data_in(in_6), .write(dec_4_16_1_s9), .data_out(out_13), .CLK(CLK), .read(dec_4_16_2_s9));
  REGISTRE_4 registre_4_5 (.data_in(in_6), .write(dec_4_16_1_s2), .data_out(out_13), .CLK(CLK), .read(dec_4_16_2_s2));
  REGISTRE_4 registre_4_6 (.data_in(in_6), .write(dec_4_16_1_s10), .data_out(out_13), .CLK(CLK), .read(dec_4_16_2_s10));
  REGISTRE_4 registre_4_7 (.data_in(in_6), .write(dec_4_16_1_s3), .data_out(out_13), .CLK(CLK), .read(dec_4_16_2_s3));
  REGISTRE_4 registre_4_8 (.data_in(in_6), .write(dec_4_16_1_s11), .data_out(out_13), .CLK(CLK), .read(dec_4_16_2_s11));
  REGISTRE_4 registre_4_9 (.data_in(in_6), .write(dec_4_16_1_s4), .data_out(out_13), .CLK(CLK), .read(dec_4_16_2_s4));
  REGISTRE_4 registre_4_10 (
    .data_in(in_6), .write(dec_4_16_1_s12), .data_out(out_13), .CLK(CLK), .read(dec_4_16_2_s12));
  REGISTRE_4 registre_4_11 (.data_in(in_6), .write(dec_4_16_1_s5), .data_out(out_13), .CLK(CLK), .read(dec_4_16_2_s5));
  REGISTRE_4 registre_4_12 (
    .data_in(in_6), .write(dec_4_16_1_s13), .data_out(out_13), .CLK(CLK), .read(dec_4_16_2_s13));
  REGISTRE_4 registre_4_13 (.data_in(in_6), .write(dec_4_16_1_s6), .data_out(out_13), .CLK(CLK), .read(dec_4_16_2_s6));
  REGISTRE_4 registre_4_14 (
    .data_in(in_6), .write(dec_4_16_1_s14), .data_out(out_13), .CLK(CLK), .read(dec_4_16_2_s14));
  REGISTRE_4 registre_4_15 (.data_in(in_6), .write(dec_4_16_1_s7), .data_out(out_13), .CLK(CLK), .read(dec_4_16_2_s7));
  REGISTRE_4 registre_4_16 (
    .data_in(in_6), .write(dec_4_16_1_s15), .data_out(out_13), .CLK(CLK), .read(dec_4_16_2_s15));
endmodule

module MEMOIRE_12b_16l (
  input  in_1,
  input  in_2,
  input  in_3,
  input  in_4,
  input  in_5,
  input  [11:0] in_6,
  input  CLK,
  input  in_8,
  input  in_9,
  input  in_10,
  input  in_11,
  input  in_12,
  output [11:0] out_13
);

  wire dec_4_16_1_s0, dec_4_16_1_s1, dec_4_16_1_s2, dec_4_16_1_s3, dec_4_16_1_s4, dec_4_16_1_s5,
       dec_4_16_1_s6, dec_4_16_1_s7, dec_4_16_1_s8, dec_4_16_1_s9, dec_4_16_1_s10, dec_4_16_1_s11,
       dec_4_16_1_s12, dec_4_16_1_s13, dec_4_16_1_s14, dec_4_16_1_s15, dec_4_16_2_s0, dec_4_16_2_s1,
       dec_4_16_2_s2, dec_4_16_2_s3, dec_4_16_2_s4, dec_4_16_2_s5, dec_4_16_2_s6, dec_4_16_2_s7,
       dec_4_16_2_s8, dec_4_16_2_s9, dec_4_16_2_s10, dec_4_16_2_s11, dec_4_16_2_s12, dec_4_16_2_s13,
       dec_4_16_2_s14, dec_4_16_2_s15;

  DEC_4_16 dec_4_16_1 (
    .s0(dec_4_16_1_s0), .s1(dec_4_16_1_s1), .s2(dec_4_16_1_s2), .s3(dec_4_16_1_s3), .s4(dec_4_16_1_s4),
    .s5(dec_4_16_1_s5), .s6(dec_4_16_1_s6), .s7(dec_4_16_1_s7), .s8(dec_4_16_1_s8), .s9(dec_4_16_1_s9),
    .s10(dec_4_16_1_s10), .s11(dec_4_16_1_s11), .s12(dec_4_16_1_s12), .s13(dec_4_16_1_s13),
    .s14(dec_4_16_1_s14), .s15(dec_4_16_1_s15), .e3(in_4), .e2(in_3), .e1(in_2), .e0(in_1), .En(in_5));
  DEC_4_16 dec_4_16_2 (
    .s0(dec_4_16_2_s0), .s1(dec_4_16_2_s1), .s2(dec_4_16_2_s2), .s3(dec_4_16_2_s3), .s4(dec_4_16_2_s4),
    .s5(dec_4_16_2_s5), .s6(dec_4_16_2_s6), .s7(dec_4_16_2_s7), .s8(dec_4_16_2_s8), .s9(dec_4_16_2_s9),
    .s10(dec_4_16_2_s10), .s11(dec_4_16_2_s11), .s12(dec_4_16_2_s12), .s13(dec_4_16_2_s13),
    .s14(dec_4_16_2_s14), .s15(dec_4_16_2_s15), .e3(in_11), .e2(in_10), .e1(in_9), .e0(in_8), .En(in_12));
  REGISTRE_12 registre_12_1 (.IN(in_6), .Write(dec_4_16_1_s0), .Read(dec_4_16_2_s0), .OUT(out_13), .CLK(CLK));
  REGISTRE_12 registre_12_2 (.IN(in_6), .Write(dec_4_16_1_s8), .Read(dec_4_16_2_s8), .OUT(out_13), .CLK(CLK));
  REGISTRE_12 registre_12_3 (.IN(in_6), .Write(dec_4_16_1_s1), .Read(dec_4_16_2_s1), .OUT(out_13), .CLK(CLK));
  REGISTRE_12 registre_12_4 (.IN(in_6), .Write(dec_4_16_1_s9), .Read(dec_4_16_2_s9), .OUT(out_13), .CLK(CLK));
  REGISTRE_12 registre_12_5 (.IN(in_6), .Write(dec_4_16_1_s2), .Read(dec_4_16_2_s2), .OUT(out_13), .CLK(CLK));
  REGISTRE_12 registre_12_6 (.IN(in_6), .Write(dec_4_16_1_s10), .Read(dec_4_16_2_s10), .OUT(out_13), .CLK(CLK));
  REGISTRE_12 registre_12_7 (.IN(in_6), .Write(dec_4_16_1_s3), .Read(dec_4_16_2_s3), .OUT(out_13), .CLK(CLK));
  REGISTRE_12 registre_12_8 (.IN(in_6), .Write(dec_4_16_1_s11), .Read(dec_4_16_2_s11), .OUT(out_13), .CLK(CLK));
  REGISTRE_12 registre_12_9 (.IN(in_6), .Write(dec_4_16_1_s4), .Read(dec_4_16_2_s4), .OUT(out_13), .CLK(CLK));
  REGISTRE_12 registre_12_10 (.IN(in_6), .Write(dec_4_16_1_s12), .Read(dec_4_16_2_s12), .OUT(out_13), .CLK(CLK));
  REGISTRE_12 registre_12_11 (.IN(in_6), .Write(dec_4_16_1_s5), .Read(dec_4_16_2_s5), .OUT(out_13), .CLK(CLK));
  REGISTRE_12 registre_12_12 (.IN(in_6), .Write(dec_4_16_1_s13), .Read(dec_4_16_2_s13), .OUT(out_13), .CLK(CLK));
  REGISTRE_12 registre_12_13 (.IN(in_6), .Write(dec_4_16_1_s6), .Read(dec_4_16_2_s6), .OUT(out_13), .CLK(CLK));
  REGISTRE_12 registre_12_14 (.IN(in_6), .Write(dec_4_16_1_s14), .Read(dec_4_16_2_s14), .OUT(out_13), .CLK(CLK));
  REGISTRE_12 registre_12_15 (.IN(in_6), .Write(dec_4_16_1_s7), .Read(dec_4_16_2_s7), .OUT(out_13), .CLK(CLK));
  REGISTRE_12 registre_12_16 (.IN(in_6), .Write(dec_4_16_1_s15), .Read(dec_4_16_2_s15), .OUT(out_13), .CLK(CLK));
endmodule

module UNITE_ADRESSAGE (
  input  [3:0] AD_in,
  input  AD_w,
  input  [3:0] PC_in,
  input  PC_w,
  input  CLK,
  output [3:0] AD_OUT,
  output [3:0] PC_OUT,
  output ext0,
  output ext1
);

  wire not_1_out;

  not not_1 (not_1_out, CLK);
  REGISTRE_4 registre_4_1 (.data_in(AD_in), .write(AD_w), .CLK(not_1_out), .read(1'b1));  // open: data_out
  REGISTRE_4 registre_4_2 (.data_in(PC_in), .write(PC_w), .data_out(PC_OUT), .CLK(CLK), .read(1'b1));

  assign AD_OUT = AD_in;
endmodule

module UNITEE_CONTROLE (
  input  CLK,
  input  [11:0] data_in,
  input  [3:0] PC_in,
  input  RESET,
  output r0b,
  output r1b,
  output r2b,
  output r3b,
  output f0,
  output f1,
  output f2,
  output ram_to_reg,
  output r0a,
  output r1a,
  output r2a,
  output reg_to_ram,
  output r3a,
  output alu_to_reg,
  output w0,
  output w1,
  output w2,
  output w3,
  output PC_write,
  output [3:0] PC_out,
  output fetch,
  output N_C,
  output N_C_2,
  output [3:0] AD_out,
  output AD_write
);

  wire [1:0] controlled_buffer_1_out, controlled_buffer_3_out;
  wire [7:0] registre_12_1_out;

  GESTION_PC gestion_pc_1 (.RESET(RESET), .PC_in(PC_in), .PC_out(PC_out), .PC_write(PC_write));
  REGISTRE_12 registre_12_1 (
    .IN(data_in), .Write(1'b1), .Read(1'b1),
    .OUT({AD_write, f2, f1, f0, registre_12_1_out[7:6], AD_out, registre_12_1_out[1:0]}), .CLK(CLK));
  // Probe on {AD_write, f2, f1, f0, registre_12_1_out[7:6], AD_out, registre_12_1_out[1:0]}
  // Probe on {AD_write, f2, f1, f0}
  // Probe on AD_out[3:2]
  // Probe on registre_12_1_out[7:6]
  // Probe on AD_out[1:0]
  // Probe on registre_12_1_out[1:0]
  and and_1 (ram_to_reg, f2, AD_write);
  and and_2 (reg_to_ram, ~f2, AD_write);  // AND_Gate
  assign controlled_buffer_1_out = ram_to_reg ? AD_out[3:2] : 2'bz;  // Controlled_Buffer controlled_buffer_1
  assign controlled_buffer_1_out = reg_to_ram ? registre_12_1_out[7:6] : 2'bz;  // Controlled_Buffer controlled_buffer_2
  assign controlled_buffer_3_out = reg_to_ram ? AD_out[3:2] : 2'bz;  // Controlled_Buffer controlled_buffer_3
  assign controlled_buffer_3_out = ram_to_reg ? registre_12_1_out[7:6] : 2'bz;  // Controlled_Buffer controlled_buffer_4
  not not_1 (alu_to_reg, AD_write);
  assign controlled_buffer_1_out = alu_to_reg ? AD_out[3:2] : 2'bz;  // Controlled_Buffer controlled_buffer_5
  assign controlled_buffer_3_out = alu_to_reg ? registre_12_1_out[7:6] : 2'bz;  // Controlled_Buffer controlled_buffer_6
  DEC_2_4 dec_2_4_1 (.s0(r0b), .s1(r1b), .s2(r2b), .s3(r3b), .e1(AD_out[1]), .e0(AD_out[0]));
  DEC_2_4 dec_2_4_2 (
    .s0(r0a), .s1(r1a), .s2(r2a), .s3(r3a), .e1(controlled_buffer_1_out[1]), .e0(controlled_buffer_1_out[0]));
  DEC_2_4 dec_2_4_3 (
    .s0(w0), .s1(w1), .s2(w2), .s3(w3), .e1(controlled_buffer_3_out[1]), .e0(controlled_buffer_3_out[0]));

  assign fetch = 1'b1;
  assign N_C_2 = N_C;
endmodule

module INCREMENTEUR_4b (
  input  [3:0] data_in,
  output [3:0] data_out,
  output R
);

  wire full_adder_1_re, full_adder_2_re, full_adder_3_re;

  FULL_ADDER full_adder_1 (.e0(1'b0), .e1(data_in[0]), .S(data_out[0]), .Ri(1'b1), .Re(full_adder_1_re));
  FULL_ADDER full_adder_2 (.e0(1'b0), .e1(data_in[1]), .S(data_out[1]), .Ri(full_adder_1_re), .Re(full_adder_2_re));
  FULL_ADDER full_adder_3 (.e0(1'b0), .e1(data_in[2]), .S(data_out[2]), .Ri(full_adder_2_re), .Re(full_adder_3_re));
  FULL_ADDER full_adder_4 (.e0(1'b0), .e1(data_in[3]), .S(data_out[3]), .Ri(full_adder_3_re), .Re(R));
endmodule

module GESTION_PC (
  input  [3:0] PC_in,
  input  RESET,
  output [3:0] PC_out,
  output PC_write
);

  wire incrementeur_4b_1_r, not_1_out;
  wire [3:0] incrementeur_4b_1_data_out;

  INCREMENTEUR_4b incrementeur_4b_1 (.data_in(PC_in), .data_out(incrementeur_4b_1_data_out), .R(incrementeur_4b_1_r));
  assign PC_out = not_1_out ? incrementeur_4b_1_data_out : 4'bz;  // Controlled_Buffer controlled_buffer_1
  assign PC_out = RESET ? {4{RESET}} : 4'bz;  // Controlled_Buffer controlled_buffer_2
  not not_1 (not_1_out, RESET);

  assign PC_write = 1'b1;
endmodule

module RAM_4b_16l (
  input  [3:0] addr,
  input  [3:0] data_in,
  input  CLK,
  input  ld___nread,
  output [3:0] data_out
);

  wire not_1_out;
  wire [3:0] ram_1_data;

  RAM #(.addrWidth(4), .dataWidth(4)) ram_1 (
    .addr(addr), .data(ram_1_data), .sel(1'b1), .clk(CLK), .ld(ld___nread), .clr(1'b0));
  assign ram_1_data = not_1_out ? data_in : 4'bz;  // Controlled_Buffer controlled_buffer_1
  not not_1 (not_1_out, ld___nread);
  assign data_out = ld___nread ? ram_1_data : 4'bz;  // Controlled_Buffer controlled_buffer_2
endmodule

module RAM_12b_16l (
  input  [3:0] addr,
  input  [11:0] data_in,
  input  CLK,
  input  ld___nread,
  output [11:0] data_out
);

  wire not_1_out;
  wire [11:0] ram_1_data;

  RAM #(.addrWidth(4), .dataWidth(12)) ram_1 (
    .addr(addr), .data(ram_1_data), .sel(1'b1), .clk(CLK), .ld(ld___nread), .clr(1'b0));
  assign ram_1_data = not_1_out ? data_in : 12'bz;  // Controlled_Buffer controlled_buffer_1
  not not_1 (not_1_out, ld___nread);
  assign data_out = ld___nread ? ram_1_data : 12'bz;  // Controlled_Buffer controlled_buffer_2
endmodule

module DEC_2_4 (
  input  e1,
  input  e0,
  output s0,
  output s1,
  output s2,
  output s3
);

  wire not_1_out, not_2_out;

  not not_1 (not_1_out, e1);
  not not_2 (not_2_out, e0);
  and and_1 (s0, not_1_out, not_2_out);
  and and_2 (s1, not_1_out, e0);
  and and_3 (s2, e1, not_2_out);
  and and_4 (s3, e1, e0);
endmodule
